# Fritzing sketch GemmaWithPixel (saved by Fritzing 0.9.2b)

parts:
  Part1 = Gemma
  LED1 = Adafruit_FLORA_RGB_Smart_Pixel

nets:
  N1: Part1.D1, LED1.connector2
  N2: Part1.GND, LED1.connector3
  N3: Part1.Vout, LED1.connector1

custom parts:
  Gemma: GEMMA is a tiny wearable platform board with a lot of might in a 1" diameter package. Powered by a Attiny85 and programmable with an Arduino IDE over USB, you'll be able to realize any wearable project!
